# Fritzing sketch Panic_Button (saved by Fritzing 0.9.3b)
circuit board: 5.40075cm x 3.7661cm
breadboards: 1

parts:
  ESP8266 = NodeMCU V3.0
  Bouton = Square Pushbutton
  R1 = Resistor [tolerance=±5% resistance=10k package="1206 [SMD]"]

nets:
  N1: ESP8266.D4, Bouton.leg1, R1.Pin_1
  N2: ESP8266.GND#6, ESP8266.GND#13, ESP8266.GND#16, ESP8266.GND#33, R1.Pin_0
  N3: ESP8266.Vin, Bouton.leg0

notes:
  Panic Button
  Dr CADIC 2016

custom parts:
  NodeMCU V3.0: ESP8266 based NodeMCU
